# Fritzing sketch Sketch (saved by Fritzing 0.9.3b)
perfboards: 1

parts:
  U1 = attiny85 [package=dip]
  WeMos_D1_Mini1 = WeMos D1 Mini
  Q1 = Basic FET P-Channel [package="D2Pak [SMD]"]
  U2 = LIPO-1000mAh [package=lipo-1000]
  C1 = Capacitor Polarized [package=panasonic_c]
  S1 = Reed switch [package=THT]
  R1 = Resistor [tolerance=±5% resistance=3.3k package="2512 [SMD]"]
  R2 = Resistor [tolerance=±5% resistance=680 package=THT]

nets:
  N1: U1.Pin_3, R2.Pin_1
  N2: U1.Pin_4, WeMos_D1_Mini1.G, U2.-, C1.-, S1.pin_1
  N3: U1.Pin_6, WeMos_D1_Mini1.D6, S1.pin_2
  N4: U1.Pin_8, Q1.source, U2.+, C1.+, R1.Pin_0
  N5: WeMos_D1_Mini1.5V, Q1.drain
  N6: WeMos_D1_Mini1.D5, Q1.Gate, R1.Pin_1, R2.Pin_0
